// Logisim project shift_reg.circ as structural Verilog: 1 circuit, main circuit main
module main (
  input  data_in,
  input  clk,
  input  rst,
  output data0,
  output data1,
  output data2,
  output data3
);

  D_Flip_Flop d_ff_1 (.D(data_in), .clk(clk), .Q(data0), .reset(rst));  // open: Qn, preset
  D_Flip_Flop d_ff_2 (.D(data0), .clk(clk), .Q(data1), .reset(rst));  // open: Qn, preset
  D_Flip_Flop d_ff_3 (.D(data1), .clk(clk), .Q(data2), .reset(rst));  // open: Qn, preset
  D_Flip_Flop d_ff_4 (.D(data2), .clk(clk), .Q(data3), .reset(rst));  // open: Qn, preset

  // Other names for the same wires on the sheet: data_out = data3
endmodule
